# Fritzing sketch Fritz_Diagram_SebastianCar  (saved by Fritzing 0.8.7b)
breadboards: 1

parts:
  Raspberry_Pi_B_rev1 = Raspberry Pi B rev2
  M1 = DC Motor
  M2 = DC Motor
  Q1 = Basic FET N-Channel [package="TO220 [THT]"]
  Q2 = Basic FET N-Channel [package="TO220 [THT]"]
  D1 = Diode [package=diode-1n4001]
  D2 = Diode [package=diode-1n4001]
  C1 = Electrolytic Capacitor [capacitance=100µF package="200 mil [THT, electrolytic]"]
  D3 = Diode [package=diode-1n4001]
  D4 = Diode [package=diode-1n4001]
  C2 = Electrolytic Capacitor [capacitance=100µF package="200 mil [THT, electrolytic]"]
  Q3 = NPN-Transistor [package="TO92 [THT]"]
  Q4 = NPN-Transistor [package="TO92 [THT]"]
  S1 = Square Pushbutton
  VCC1 = 4 x AAA Battery Mount  # not connected
  R8 = Resistor [tolerance=±5% resistance=10k package=THT]
  R9 = Resistor [tolerance=±5% resistance=5k package=THT]
  R10 = Resistor [tolerance=±5% resistance=10k package=THT]
  R11 = Resistor [tolerance=±5% resistance=10k package=THT]
  R12 = Resistor [tolerance=±5% resistance=10k package=THT]
  R13 = Resistor [tolerance=±5% resistance=5k package=THT]
  R14 = Resistor [tolerance=±5% resistance=10k package=THT]

nets:
  N1: Raspberry_Pi_B_rev1.5V, D2.A, D4.A, S1.leg0, R8.Pin_0, R10.Pin_1, R12.Pin_0, R14.Pin_1
  N2: Raspberry_Pi_B_rev1.GND, Q1.source, Q2.source, D1.C, C1.-, D3.C, C2.-, Q3.E, Q4.E, R11.Pin_1
  N3: Raspberry_Pi_B_rev1.GPIO_17, R8.Pin_1, R9.Pin_0
  N4: Raspberry_Pi_B_rev1.GPIO_4, R12.Pin_1, R13.Pin_0
  N5: Raspberry_Pi_B_rev1.GPIO_9, S1.leg1, R11.Pin_0
  N6: M1.pin_1, Q2.drain, D1.A, C1.+
  N7: M1.pin_2, M2.pin_2
  N8: M2.pin_1, Q1.drain, D3.A, C2.+
  N9: Q1.gate, Q4.C, R14.Pin_0
  N10: Q2.gate, Q3.C, R10.Pin_0
  N11: Q3.B, R9.Pin_1
  N12: Q4.B, R13.Pin_1
